// Logisim project pipline_0.1.0.circ as structural Verilog: 27 circuits, main circuit main
module main (
);

  wire alu_1_out_5, alu_1_out_6, alu_1_out_7, control_unit_1_out_14, control_unit_1_out_15,
       control_unit_1_out_16, control_unit_1_out_17, control_unit_1_out_18, control_unit_1_out_19,
       control_unit_1_out_20, control_unit_1_out_22, control_unit_1_out_23, cp0_1_out_10, decoder_out_2,
       decoder_out_3, decoder_out_4, decoder_out_7, decoder_out_8, decoder_out_9, EXMEM_out_26, EXMEM_out_27,
       EXMEM_out_28, EXMEM_out_29, EXMEM_out_34, EXMEM_out_35, EXMEM_out_45, EXMEM_out_46, idex_reg_out_12,
       idex_reg_out_14, idex_reg_out_15, idex_reg_out_17, idex_reg_out_19, idex_reg_out_20, idex_reg_out_24,
       idex_reg_out_36, idex_reg_out_37, memwb_reg_1_out_14, memwb_reg_1_out_15, memwb_reg_1_out_21,
       multiplexer_9_out, undriven, undriven_2, undriven_6, undriven_7;
  wire [1:0] control_unit_1_out_13, decoder_out_10, decoder_out_11,
       \forwarding_unit_1_a_sel用于选择使用哪一个转发数据_或默认原始数据 , \forwarding_unit_1_fu_sel__用于选择使用哪一个转发数据_或默认原始数据 ,
       idex_reg_out_16, idex_reg_out_21, n32_2_1_out_2, n32_2_2_out_2;
  wire [2:0] EXMEM_out_30, EXMEM_out_40, idex_reg_out_13, idex_reg_out_25, idex_reg_out_26;
  wire [3:0] EXMEM_out_42, EXMEM_out_43, idex_reg_out_18, lw_reg_b_w_e_gen_1_out_3, memwb_reg_1_out_17,
       sw_mem_b_w_e_gen_1_out_3;
  wire [4:0] control_unit_1_out_24, decoder_out_6, EXMEM_out_39, EXMEM_out_44, idex_reg_out_23,
       idex_reg_out_27, idex_reg_out_28, idex_reg_out_29, idex_reg_out_35, ifid_reg_out_11, ifid_reg_out_12,
       ifid_reg_out_13, memwb_reg_1_out_16, memwb_reg_1_out_20, multiplexer_2_out, multiplexer_4_out,
       multiplexer_7_out, n32_5_1_out_2, undriven_4, undriven_5;
  wire [15:0] ifid_reg_out_14;
  wire [31:0] adder_1_out, adder_2_out, alu_1_out_4, barrel_shifter_1_out_4,
       branch_predict_unit_1_predicted_pc, control_unit_1_out_25, cp0_1_out_9, cp0_1_out_11,
       data_mem_interface_out_7, EXMEM_out_31, EXMEM_out_32, EXMEM_out_33, EXMEM_out_37, EXMEM_out_38,
       final_target_1_out_7, \forwarding_unit_1_input_a_根据写使能修改后的wb的转发数据 ,
       \forwarding_unit_1_input_b_根据写使能修改后的wb的转发数据 , GPR_out_9, GPR_out_10, idex_reg_out_30, idex_reg_out_31,
       idex_reg_out_32, idex_reg_out_33, idex_reg_out_34, ifid_reg_out_10, ifid_reg_out_15, ifid_reg_out_16,
       ifid_reg_out_17, instr_mem_interface_out_4, mem_r_data_shift_1_out_4, memwb_reg_1_out_18,
       memwb_reg_1_out_19, memwb_reg_1_out_22, multiplexer_1_out, multiplexer_3_out, multiplexer_5_out,
       multiplexer_6_out, multiplexer_8_out, multiplexer_10_out, multiplexer_11_out, PC_out_5,
       real_rt_data_gen_1_out_4, undriven_3, \位扩展单元_out_3 ;

  branch_predict_unit branch_predict_unit_1 (
    .current_pc(PC_out_5), .next_pc(final_target_1_out_7), .bpu_write_en(control_unit_1_out_22),
    .tag_pc(EXMEM_out_32), .predicted_pc(branch_predict_unit_1_predicted_pc));
  pc PC (.in_2(undriven), .in_4(multiplexer_1_out), .out_5(PC_out_5), .in_3(undriven_2), .in_1(control_unit_1_out_14));
  Multiplexer #(.select(2), .width(32), .enable("false")) multiplexer_1 (
    .in0(ifid_reg_out_10), .in1(branch_predict_unit_1_predicted_pc), .in2(cp0_1_out_11), .in3(adder_1_out),
    .out(multiplexer_1_out), .sel(control_unit_1_out_13));
  instr_mem_interface instr_mem_interface (
    .in_3(PC_out_5), .out_4(instr_mem_interface_out_4));  // open: in_1, in_2, out_5
  Adder #(.width(32)) adder_1 (.a(undriven_3), .b(PC_out_5), .out(adder_1_out));  // open: cin, cout
  ifid_reg ifid_reg (
    .in_1(undriven), .in_2(undriven_2), .in_3(control_unit_1_out_15), .in_4(control_unit_1_out_16),
    .in_5(PC_out_5), .in_6(adder_1_out), .in_7(instr_mem_interface_out_4), .out_10(ifid_reg_out_10),
    .out_11(ifid_reg_out_11), .out_12(ifid_reg_out_12), .out_14(ifid_reg_out_14), .out_15(ifid_reg_out_15),
    .out_16(ifid_reg_out_16), .out_17(ifid_reg_out_17), .out_13(ifid_reg_out_13));  // open: in_8, in_9, out_18, out_19
  decoder decoder (
    .in_1(ifid_reg_out_15), .out_7(decoder_out_7), .out_8(decoder_out_8), .out_9(decoder_out_9),
    .out_10(decoder_out_10), .out_6(decoder_out_6), .out_4(decoder_out_4), .out_3(decoder_out_3),
    .out_2(decoder_out_2), .out_11(decoder_out_11));  // open: out_5
  Multiplexer #(.width(5), .enable("false")) multiplexer_2 (
    .in0(ifid_reg_out_12), .in1(undriven_4), .out(multiplexer_2_out), .sel(decoder_out_9));
  GPR GPR (
    .in_1(undriven), .in_2(undriven_2), .in_3(ifid_reg_out_11), .in_4(multiplexer_2_out),
    .in_5(memwb_reg_1_out_16), .in_6(memwb_reg_1_out_14), .in_7(multiplexer_11_out),
    .in_8(memwb_reg_1_out_17), .out_9(GPR_out_9), .out_10(GPR_out_10));
  imm_ext \u_位扩展单元  (.in_1(ifid_reg_out_14), .in_2(decoder_out_10), .out_3(\位扩展单元_out_3 ));
  Multiplexer #(.width(32), .enable("false")) multiplexer_3 (
    .in0(cp0_1_out_9), .in1(GPR_out_10), .out(multiplexer_3_out), .sel(decoder_out_4));
  control_unit control_unit_1 (
    .in_8(idex_reg_out_33), .in_9(final_target_1_out_7), .in_3(EXMEM_out_46), .out_17(control_unit_1_out_17),
    .out_15(control_unit_1_out_15), .out_18(control_unit_1_out_18), .in_2(decoder_out_7),
    .out_14(control_unit_1_out_14), .out_16(control_unit_1_out_16), .in_5(ifid_reg_out_11),
    .in_7(idex_reg_out_29), .out_19(control_unit_1_out_19), .out_20(control_unit_1_out_20),
    .out_22(control_unit_1_out_22), .in_6(multiplexer_2_out), .in_10(cp0_1_out_10), .in_11(decoder_out_2),
    .in_12(decoder_out_3), .out_23(control_unit_1_out_23), .out_24(control_unit_1_out_24),
    .out_25(control_unit_1_out_25), .out_13(control_unit_1_out_13));  // open: in_4, in_1, out_21, out_26
  Multiplexer #(.select(2), .width(5), .enable("false")) multiplexer_4 (
    .in0(ifid_reg_out_12), .in1(ifid_reg_out_13), .in2(undriven_5), .out(multiplexer_4_out),
    .sel(decoder_out_11));  // open: in3
  idex_reg idex_reg (
    .ctrl_from_id(undriven), .stall(undriven_2), .flush(control_unit_1_out_17), .clk(control_unit_1_out_18),
    .reset(decoder_out_8), .PC(ifid_reg_out_16), .rs_from_reg(GPR_out_9), .rt_from_reg(multiplexer_3_out),
    .imm_extended(\位扩展单元_out_3 ), .out_12(idex_reg_out_12), .out_13(idex_reg_out_13),
    .out_14(idex_reg_out_14), .out_25(idex_reg_out_25), .out_15(idex_reg_out_15), .out_16(idex_reg_out_16),
    .out_17(idex_reg_out_17), .out_18(idex_reg_out_18), .out_20(idex_reg_out_20), .out_21(idex_reg_out_21),
    .out_24(idex_reg_out_24), .out_27(idex_reg_out_27), .out_28(idex_reg_out_28), .out_29(idex_reg_out_29),
    .out_30(idex_reg_out_30), .out_31(idex_reg_out_31), .out_32(idex_reg_out_32), .out_23(idex_reg_out_23),
    .PC_2(ifid_reg_out_17), .out_33(idex_reg_out_33), .out_34(idex_reg_out_34), .out_26(idex_reg_out_26),
    .out_19(idex_reg_out_19), .in_11(multiplexer_4_out), .out_35(idex_reg_out_35), .out_36(idex_reg_out_36),
    .out_37(idex_reg_out_37));  // open: out_22
  forwarding_unit forwarding_unit_1 (
    .\rs_data_rs的原始输入 (idex_reg_out_30), .\rt_data_rt的原始输入 (idex_reg_out_31),
    .\memwb_byte_en_对齐处理后的写使能 (EXMEM_out_42), .rs_addr(idex_reg_out_27), .rt_addr(idex_reg_out_28),
    .memwb_rd_addr(memwb_reg_1_out_16),
    .\input_A_根据写使能修改后的wb的转发数据 (\forwarding_unit_1_input_a_根据写使能修改后的wb的转发数据 ),
    .\input_B_根据写使能修改后的wb的转发数据 (\forwarding_unit_1_input_b_根据写使能修改后的wb的转发数据 ),
    .\fu_sel__用于选择使用哪一个转发数据_或默认原始数据 (\forwarding_unit_1_fu_sel__用于选择使用哪一个转发数据_或默认原始数据 ),
    .\memwb_data_转发数据 (multiplexer_11_out),
    .\A_sel用于选择使用哪一个转发数据_或默认原始数据 (\forwarding_unit_1_a_sel用于选择使用哪一个转发数据_或默认原始数据 ),
    .exmem_rd_addr(EXMEM_out_39), .\exmem_byte_en_对齐处理后的写使能 (memwb_reg_1_out_17));
  Multiplexer #(.select(2), .width(32), .enable("false")) multiplexer_5 (
    .in0(idex_reg_out_30), .in1(EXMEM_out_37), .in2(\forwarding_unit_1_input_a_根据写使能修改后的wb的转发数据 ),
    .out(multiplexer_5_out), .sel(\forwarding_unit_1_fu_sel__用于选择使用哪一个转发数据_或默认原始数据 ));  // open: in3
  Multiplexer #(.select(2), .width(32), .enable("false")) multiplexer_6 (
    .in0(idex_reg_out_31), .in1(EXMEM_out_37), .in2(\forwarding_unit_1_input_b_根据写使能修改后的wb的转发数据 ),
    .out(multiplexer_6_out), .sel(\forwarding_unit_1_a_sel用于选择使用哪一个转发数据_或默认原始数据 ));  // open: in3
  _32_5 u_32_5_1 (.in_1(multiplexer_6_out), .out_2(n32_5_1_out_2));
  Multiplexer #(.width(5), .enable("false")) multiplexer_7 (
    .in0(idex_reg_out_23), .in1(n32_5_1_out_2), .out(multiplexer_7_out), .sel(idex_reg_out_24));
  Multiplexer #(.width(32), .enable("false")) multiplexer_8 (
    .in0(multiplexer_6_out), .in1(idex_reg_out_32), .out(multiplexer_8_out), .sel(idex_reg_out_20));
  ALU alu_1 (
    .in_2(multiplexer_5_out), .in_3(multiplexer_8_out), .in_1(idex_reg_out_18), .out_4(alu_1_out_4),
    .out_5(alu_1_out_5), .out_6(alu_1_out_6), .out_7(alu_1_out_7));
  barrel_shifter barrel_shifter_1 (
    .in_1(multiplexer_7_out), .in_2(idex_reg_out_21), .in_3(multiplexer_6_out), .out_4(barrel_shifter_1_out_4));
  Multiplexer #(.enable("false")) multiplexer_9 (
    .in0(idex_reg_out_17), .in1(undriven_6), .out(multiplexer_9_out), .sel(undriven_7));
  // AND_Gate and_1 has open pins: in0=alu_1_out_7, in1=idex_reg_out_19, out=open
  _32_2 u_32_2_1 (.in_1(alu_1_out_4), .out_2(n32_2_1_out_2));
  Adder #(.width(32)) adder_2 (.a(idex_reg_out_32), .b(idex_reg_out_34), .out(adder_2_out));  // open: cin, cout
  lw_reg_b_w_e_gen lw_reg_b_w_e_gen_1 (.in_1(n32_2_1_out_2), .in_2(idex_reg_out_25), .out_3(lw_reg_b_w_e_gen_1_out_3));
  sw_mem_b_w_e_gen sw_mem_b_w_e_gen_1 (.in_1(n32_2_1_out_2), .in_2(idex_reg_out_26), .out_3(sw_mem_b_w_e_gen_1_out_3));
  real_rt_data_gen real_rt_data_gen_1 (
    .in_1(n32_2_1_out_2), .in_2(idex_reg_out_26), .in_3(multiplexer_6_out), .out_4(real_rt_data_gen_1_out_4));
  exmem_reg EXMEM (
    .\_4个通用控制信号 (undriven), .in_2(idex_reg_out_12), .in_3(undriven_2), .in_4(idex_reg_out_13),
    .in_5(control_unit_1_out_19), .in_6(control_unit_1_out_20), .in_7(adder_2_out),
    .\_3个读写控制 (idex_reg_out_14), .in_9(idex_reg_out_33), .in_10(idex_reg_out_15), .in_11(multiplexer_9_out),
    .in_12(idex_reg_out_34), .\ALU的3个flag (alu_1_out_5), .in_14(alu_1_out_6), .in_15(alu_1_out_7),
    .in_16(multiplexer_10_out), .in_17(real_rt_data_gen_1_out_4), .in_18(idex_reg_out_29),
    .in_19(idex_reg_out_25), .out_26(EXMEM_out_26), .out_27(EXMEM_out_27), .out_28(EXMEM_out_28),
    .out_30(EXMEM_out_30), .out_29(EXMEM_out_29), .out_31(EXMEM_out_31), .out_32(EXMEM_out_32),
    .out_33(EXMEM_out_33), .out_34(EXMEM_out_34), .out_35(EXMEM_out_35), .out_38(EXMEM_out_38),
    .out_37(EXMEM_out_37), .out_39(EXMEM_out_39), .out_40(EXMEM_out_40), .in_21(sw_mem_b_w_e_gen_1_out_3),
    .in_22(lw_reg_b_w_e_gen_1_out_3), .out_42(EXMEM_out_42), .out_43(EXMEM_out_43), .in_23(idex_reg_out_35),
    .in_24(idex_reg_out_36), .in_25(idex_reg_out_37), .out_44(EXMEM_out_44), .out_45(EXMEM_out_45),
    .out_46(EXMEM_out_46));  // open: out_36, in_20, out_41
  Multiplexer #(.select(2), .width(32), .enable("false")) multiplexer_10 (
    .in0(alu_1_out_4), .in1(barrel_shifter_1_out_4), .out(multiplexer_10_out), .sel(idex_reg_out_16));  // open: in2, in3
  cp0 cp0_1 (
    .in_1(control_unit_1_out_23), .in_2(control_unit_1_out_24), .in_3(memwb_reg_1_out_21),
    .in_4(memwb_reg_1_out_20), .in_5(memwb_reg_1_out_22), .in_7(decoder_out_6), .in_8(control_unit_1_out_25),
    .out_9(cp0_1_out_9), .out_10(cp0_1_out_10), .out_11(cp0_1_out_11));  // open: in_6
  data_mem_interface data_mem_interface (
    .in_2(EXMEM_out_27), .in_4(EXMEM_out_37), .in_5(EXMEM_out_38), .out_7(data_mem_interface_out_7),
    .in_1(EXMEM_out_26), .in_6(EXMEM_out_43));  // open: in_3, out_8
  final_target final_target_1 (
    .in_1(EXMEM_out_29), .in_2(EXMEM_out_30), .in_3(EXMEM_out_35), .in_4(EXMEM_out_34), .in_5(EXMEM_out_33),
    .in_6(EXMEM_out_31), .out_7(final_target_1_out_7));
  _32_2 u_32_2_2 (.in_1(EXMEM_out_37), .out_2(n32_2_2_out_2));
  mem_r_data_shift mem_r_data_shift_1 (
    .in_1(n32_2_2_out_2), .in_2(EXMEM_out_40), .in_3(data_mem_interface_out_7),
    .out_4(mem_r_data_shift_1_out_4));
  memwb_reg memwb_reg_1 (
    .in_1(undriven), .in_2(undriven_2), .in_5(EXMEM_out_27), .in_6(EXMEM_out_28), .in_7(EXMEM_out_39),
    .in_8(EXMEM_out_42), .in_9(mem_r_data_shift_1_out_4), .in_10(EXMEM_out_37), .out_14(memwb_reg_1_out_14),
    .out_15(memwb_reg_1_out_15), .out_16(memwb_reg_1_out_16), .out_17(memwb_reg_1_out_17),
    .out_18(memwb_reg_1_out_18), .out_19(memwb_reg_1_out_19), .in_11(EXMEM_out_44), .in_12(EXMEM_out_45),
    .out_20(memwb_reg_1_out_20), .out_21(memwb_reg_1_out_21), .in_13(EXMEM_out_38),
    .out_22(memwb_reg_1_out_22));  // open: in_3, in_4
  Multiplexer #(.width(32), .enable("false")) multiplexer_11 (
    .in0(memwb_reg_1_out_18), .in1(memwb_reg_1_out_19), .out(multiplexer_11_out), .sel(memwb_reg_1_out_15));

  // Notes on the sheet:
  //   1
  //   4
  //   5'b0000
  //   byte_en
  //   addr
  //   write
  //   data
  //   5'b11111
  //   Rd_addr_sel
  //   shift_amount_sel
  //   Rt_imm_sel
  //   ALU
  //   Barrel Shifter
  //   0
  //   calculate_branch_addr
  //   Exec_res_sel
endmodule

module ifid_reg (
  input  in_1,
  input  in_2,
  input  in_3,
  input  in_4,
  input  [31:0] in_5,
  input  [31:0] in_6,
  input  [31:0] in_7,
  input  in_8,
  input  [4:0] in_9,
  output [31:0] out_10,
  output [4:0] out_11,
  output [4:0] out_12,
  output [4:0] out_13,
  output [15:0] out_14,
  output [31:0] out_15,
  output [31:0] out_16,
  output [31:0] out_17,
  output out_18,
  output [4:0] out_19
);
endmodule

module decoder (
  input  [31:0] in_1,
  output out_2,
  output out_3,
  output out_4,
  output out_5,
  output [4:0] out_6,
  output out_7,
  output out_8,
  output out_9,
  output [1:0] out_10,
  output [1:0] out_11
);
endmodule

module idex_reg (
  input  clk,
  input  reset,
  input  stall,
  input  flush,
  input  ctrl_from_id,
  input  [31:0] PC,
  input  [31:0] rs_from_reg,
  input  [31:0] rt_from_reg,
  input  [31:0] imm_extended,
  input  [31:0] PC_2,
  input  [4:0] in_11,
  output out_12,
  output [2:0] out_13,
  output out_14,
  output out_15,
  output [1:0] out_16,
  output out_17,
  output [3:0] out_18,
  output out_19,
  output out_20,
  output [1:0] out_21,
  output out_22,
  output [4:0] out_23,
  output out_24,
  output [2:0] out_25,
  output [2:0] out_26,
  output [4:0] out_27,
  output [4:0] out_28,
  output [4:0] out_29,
  output [31:0] out_30,
  output [31:0] out_31,
  output [31:0] out_32,
  output [31:0] out_33,
  output [31:0] out_34,
  output [4:0] out_35,
  output out_36,
  output out_37
);
endmodule

module exmem_reg (
  input  \_4个通用控制信号 ,
  input  in_2,
  input  in_3,
  input  [2:0] in_4,
  input  in_5,
  input  in_6,
  input  [31:0] in_7,
  input  \_3个读写控制 ,
  input  [31:0] in_9,
  input  in_10,
  input  in_11,
  input  [31:0] in_12,
  input  \ALU的3个flag ,
  input  in_14,
  input  in_15,
  input  [31:0] in_16,
  input  [31:0] in_17,
  input  [4:0] in_18,
  input  [2:0] in_19,
  input  [2:0] in_20,
  input  [3:0] in_21,
  input  [3:0] in_22,
  input  [4:0] in_23,
  input  in_24,
  input  in_25,
  output out_26,
  output out_27,
  output out_28,
  output out_29,
  output [2:0] out_30,
  output [31:0] out_31,
  output [31:0] out_32,
  output [31:0] out_33,
  output out_34,
  output out_35,
  output out_36,
  output [31:0] out_37,
  output [31:0] out_38,
  output [4:0] out_39,
  output [2:0] out_40,
  output [1:0] out_41,
  output [3:0] out_42,
  output [3:0] out_43,
  output [4:0] out_44,
  output out_45,
  output out_46
);


  // Notes on the sheet:
  //   3个分支相关
endmodule

module memwb_reg (
  input  in_1,
  input  in_2,
  input  in_3,
  input  in_4,
  input  in_5,
  input  in_6,
  input  [4:0] in_7,
  input  [3:0] in_8,
  input  [31:0] in_9,
  input  [31:0] in_10,
  input  [4:0] in_11,
  input  in_12,
  input  [31:0] in_13,
  output out_14,
  output out_15,
  output [4:0] out_16,
  output [3:0] out_17,
  output [31:0] out_18,
  output [31:0] out_19,
  output [4:0] out_20,
  output out_21,
  output [31:0] out_22
);
endmodule

module ALU (
  input  [3:0] in_1,
  input  [31:0] in_2,
  input  [31:0] in_3,
  output [31:0] out_4,
  output out_5,
  output out_6,
  output out_7
);
endmodule

module lw_reg_b_w_e_gen (
  input  [1:0] in_1,
  input  [2:0] in_2,
  output [3:0] out_3
);
endmodule

module sw_mem_b_w_e_gen (
  input  [1:0] in_1,
  input  [2:0] in_2,
  output [3:0] out_3
);
endmodule

module real_rt_data_gen (
  input  [1:0] in_1,
  input  [2:0] in_2,
  input  [31:0] in_3,
  output [31:0] out_4
);
endmodule

module barrel_shifter (
  input  [4:0] in_1,
  input  [1:0] in_2,
  input  [31:0] in_3,
  output [31:0] out_4
);
endmodule

// rt_sel
module rt_data_sel (
  input  [31:0] in_1,
  output [31:0] out_2
);
endmodule

// rs_sel
module rs_data_sel (
  input  [31:0] in_1,
  output [31:0] out_2
);
endmodule

module _32_2 (
  input  [31:0] in_1,
  output [1:0] out_2
);
endmodule

module _32_5 (
  input  [31:0] in_1,
  output [4:0] out_2
);
endmodule

module GPR (
  input  in_1,
  input  in_2,
  input  [4:0] in_3,
  input  [4:0] in_4,
  input  [4:0] in_5,
  input  in_6,
  input  [31:0] in_7,
  input  [3:0] in_8,
  output [31:0] out_9,
  output [31:0] out_10
);
endmodule

module data_mem_interface (
  input  in_1,
  input  in_2,
  input  in_3,
  input  [31:0] in_4,
  input  [31:0] in_5,
  input  [3:0] in_6,
  output [31:0] out_7,
  output out_8
);
endmodule

module mem_r_data_shift (
  input  [1:0] in_1,
  input  [2:0] in_2,
  input  [31:0] in_3,
  output [31:0] out_4
);
endmodule

module final_target (
  input  in_1,
  input  [2:0] in_2,
  input  in_3,
  input  in_4,
  input  [31:0] in_5,
  input  [31:0] in_6,
  output [31:0] out_7
);
endmodule

module instr_mem_interface (
  input  in_1,
  input  in_2,
  input  [31:0] in_3,
  output [31:0] out_4,
  output out_5
);
endmodule

module pc (
  input  in_1,
  input  in_2,
  input  in_3,
  input  [31:0] in_4,
  output [31:0] out_5
);
endmodule

module imm_ext (
  input  [15:0] in_1,
  input  [1:0] in_2,
  output [31:0] out_3
);
endmodule

module control_unit (
  input  in_1,
  input  in_2,
  input  in_3,
  input  in_4,
  input  [4:0] in_5,
  input  [4:0] in_6,
  input  [4:0] in_7,
  input  [31:0] in_8,
  input  [31:0] in_9,
  input  in_10,
  input  in_11,
  input  in_12,
  output [1:0] out_13,
  output out_14,
  output out_15,
  output out_16,
  output out_17,
  output out_18,
  output out_19,
  output out_20,
  output out_21,
  output out_22,
  output out_23,
  output [4:0] out_24,
  output [31:0] out_25,
  output [31:0] out_26
);
endmodule

module forwarding_unit (
  input  [31:0] \rs_data_rs的原始输入 ,
  input  [31:0] \rt_data_rt的原始输入 ,
  input  [3:0] \memwb_byte_en_对齐处理后的写使能 ,
  input  [3:0] \exmem_byte_en_对齐处理后的写使能 ,
  input  [4:0] rs_addr,
  input  [4:0] rt_addr,
  input  [4:0] exmem_rd_addr,
  input  [4:0] memwb_rd_addr,
  input  [31:0] \memwb_data_转发数据 ,
  output [31:0] \input_A_根据写使能修改后的wb的转发数据 ,
  output [31:0] \input_B_根据写使能修改后的wb的转发数据 ,
  output [1:0] \fu_sel__用于选择使用哪一个转发数据_或默认原始数据 ,
  output [1:0] \A_sel用于选择使用哪一个转发数据_或默认原始数据 
);


  // Notes on the sheet:
  //   如果写使能全无效，不考虑转发MEMWB
  //   如果写使能全无效，不考虑转发EXMEM
endmodule

module branch_predict_unit (
  input  [31:0] current_pc,
  input  [31:0] tag_pc,
  input  [31:0] next_pc,
  input  bpu_write_en,
  output [31:0] predicted_pc
);
endmodule

module cp0 (
  input  in_1,
  input  [4:0] in_2,
  input  in_3,
  input  [4:0] in_4,
  input  [31:0] in_5,
  input  in_6,
  input  [4:0] in_7,
  input  [31:0] in_8,
  output [31:0] out_9,
  output out_10,
  output [31:0] out_11
);
endmodule

module exception (
  input  in_1,
  input  [31:0] in_2,
  output out_3,
  output [4:0] out_4
);
endmodule
